# Fritzing sketch Schematic (saved by Fritzing 0.9.3b)

parts:
  VALVE1 = Plastic Solenoid Valve
  VALVE2 = Plastic Solenoid Valve
  VALVE3 = Plastic Solenoid Valve
  VALVE4 = Plastic Solenoid Valve
  U1 = 4-Channel 5v Relay Shield [package=relay-4ch5v10a]
  Squix1 = OLED 0.96" 128x64 I2C SSD1306
  S1 = Round Pushbutton
  S2 = Round Pushbutton
  S3 = Round Pushbutton
  Bauteil1 = Arduino Nano (Rev3.0)
  LM1 = RioRand LM2596
  LM2 = RioRand LM2596
  D1 = Diode [package=diode-1n4001]
  D2 = Diode [package=diode-1n4001]
  D3 = Diode [package=diode-1n4001]
  D4 = Diode [package=diode-1n4001]
  S4 = Taiway 100-SP-X-T1 SPDT Miniature Toggle Switch [part_number=100-SP-X-T1-0-0-B1-M1 package=THT]
  U2 = LIPO-2000mAh [package=lipo-2000]
  U3 = LIPO-2000mAh [package=lipo-2000]
  U4 = LIPO-2000mAh [package=lipo-2000]
  METER1 = 7-Segment Panel Voltmeter

nets:
  N1: VALVE1.no_name_yet#1, U1.K1-Off, D1.C
  N2: VALVE1.no_name_yet#2, VALVE2.no_name_yet#2, VALVE3.no_name_yet#2, VALVE4.no_name_yet#2, D1.A, D2.A, D3.A, D4.A, U2.-, METER1.V-
  N3: VALVE2.no_name_yet#1, U1.K2-Off, D2.C
  N4: VALVE3.no_name_yet#1, U1.K3-Off, D3.C
  N5: VALVE4.no_name_yet#1, U1.K4-Off, D4.C
  VCC: U1.VCC, Squix1.VCC, Bauteil1.5V
  N6: U1.GND, LM2.Pin_3
  N7: U1.IN1, Bauteil1.D2
  N8: U1.IN2, Bauteil1.D3
  N9: U1.K1-On, U1.K2-On, U1.K3-On, U1.K4-On, S4.L1, METER1.V+
  N10: U1.IN4, Bauteil1.D5
  N11: U1.IN3, Bauteil1.D4
  GND: Squix1.GND, S1.leg1, S2.leg1, S3.leg1, Bauteil1.GND, LM1.Pin_3
  N12: Squix1.SCL, Bauteil1.A5
  N13: Squix1.SCA, Bauteil1.A4
  N14: S1.leg0, Bauteil1.D10
  N15: S2.leg0, Bauteil1.D9
  N16: S3.leg0, Bauteil1.D8
  N17: Bauteil1.VIN, LM1.Pin_2
  N18: S4.L2, U4.+
  N19: U2.+, U3.-
  N20: U3.+, U4.-

notes:
  5V Relais Power
  Remove Jumper to enable Optocoupling
  5V Arduino Power
  3S LiPo / 12V Battery / Power Supply
  Also add some capacitors on various locations on the different supply voltage lines!

custom parts:
  4-Channel 5v Relay Shield: 4 Channel 5v Relay Shield w. 2x SPD-06VDC-SD-C
  7-Segment Panel Voltmeter: 7-Segment Panel Voltmeter (4.5 - 30V)
